# Fritzing sketch mobile-main (saved by Fritzing 0.9.3b)
circuit board: 10.4454cm x 12.0136cm
breadboards: 1

parts:
  Arduino_Mega2560 = Arduino Mega 2560 (Rev3)
  Reset_Button = Pushbutton [package="[THT]"]
  IR_Sensor_Header = female pin header, 8 pins [form="♀ (female)"]
  HC-12 = HC-12 Connector [form="♀ (female)" package=THT]
  J1 = female pin header, 18 pins [form="♀ (female)"]
  J2 = female pin header, 18 pins [form="♀ (female)"]
  J3 = female pin header, 4 pins [form="♀ (female)"]
  TCS34725 = Generic female header - 7 pins [form="♀ (female)" package=THT]
  J4 = female pin header, 2 pins [form="♀ (female)"]
  J5 = female pin header, 2 pins [form="♀ (female)"]
  L293D = L293D [package=THT]
  J6 = Camdenboss CTB0158-2 [part_number=CTB0158-2 package=THT]
  J7 = Camdenboss CTB0158-2 [part_number=CTB0158-2 package=THT]
  J8 = female pin header, 1 pin [form="♀ (female)"]
  S1 = Pushbutton [package="[THT]"]
  S2 = Pushbutton [package="[THT]"]
  S3 = Pushbutton [package="[THT]"]
  S4 = Pushbutton [package="[THT]"]
  J9 = female pin header, 2 pins [form="♀ (female)"]
  J10 = female pin header, 2 pins [form="♀ (female)"]
  SG1 = Buzzer 12mm [package=buzzer-ccv]

nets:
  N1: Arduino_Mega2560.A8, SG1.2
  N2: Arduino_Mega2560.A0, IR_Sensor_Header.pin8
  N3: Arduino_Mega2560.A1, IR_Sensor_Header.pin7
  N4: Arduino_Mega2560.A2, IR_Sensor_Header.pin6
  N5: Arduino_Mega2560.A3, IR_Sensor_Header.pin5
  N6: Arduino_Mega2560.A4, IR_Sensor_Header.pin4
  N7: Arduino_Mega2560.A5, IR_Sensor_Header.pin3
  N8: Arduino_Mega2560.A6, IR_Sensor_Header.pin2
  N9: Arduino_Mega2560.A7, IR_Sensor_Header.pin1
  N10: Arduino_Mega2560.D21/SCL, Arduino_Mega2560.SCL, TCS34725.SCL, J4.pin1, J5.pin1
  N11: Arduino_Mega2560.D20/SDA, Arduino_Mega2560.SDA, TCS34725.SDA, J4.pin2, J5.pin2
  N12: Arduino_Mega2560.D15/RX3, HC-12.Rx#3
  N13: Arduino_Mega2560.D14/TX3, HC-12.Rx#2
  GND: Arduino_Mega2560.GND, Reset_Button.Pin_3, Reset_Button.Pin_4, HC-12.GND, J1.pin18, J2.pin18, J3.pin3, TCS34725.GND, L293D.0V, S1.Pin_1, S1.Pin_2, S2.Pin_3, S2.Pin_4, S3.Pin_3, S3.Pin_4, S4.Pin_1, S4.Pin_2, J9.pin2
  N14: Arduino_Mega2560.D13_PWM, L293D.In_2
  N15: Arduino_Mega2560.D11_PWM, L293D.In_1
  N16: Arduino_Mega2560.D10_PWM, L293D.In_4
  N17: Arduino_Mega2560.D9_PWM, L293D.Enable_2
  N18: Arduino_Mega2560.D8_PWM, L293D.In_3
  N19: Arduino_Mega2560.RESET, Reset_Button.Pin_1, Reset_Button.Pin_2
  5V: Arduino_Mega2560.5V, HC-12.Vcc, J1.pin1, J2.pin1, J3.pin4, TCS34725.Vin, L293D.+V
  N20: Arduino_Mega2560.D0_RX0, J10.pin1
  N21: Arduino_Mega2560.D1_TX0, J10.pin2
  N22: Arduino_Mega2560.D4_PWM, S4.Pin_3, S4.Pin_4
  N23: Arduino_Mega2560.D5_PWM, S1.Pin_3, S1.Pin_4
  N24: Arduino_Mega2560.D6_PWM, S3.Pin_1, S3.Pin_2
  N25: Arduino_Mega2560.D7_PWM, S2.Pin_1, S2.Pin_2
  N26: Arduino_Mega2560.D22, J2.pin2
  N27: Arduino_Mega2560.D23, J1.pin2
  N28: Arduino_Mega2560.D24, J2.pin3
  N29: Arduino_Mega2560.D25, J1.pin3
  N30: Arduino_Mega2560.D26, J2.pin4
  N31: Arduino_Mega2560.D27, J1.pin4
  N32: Arduino_Mega2560.D28, J2.pin5
  N33: Arduino_Mega2560.D29, J1.pin5
  N34: Arduino_Mega2560.D30, J2.pin6
  N35: Arduino_Mega2560.D31, J1.pin6
  N36: Arduino_Mega2560.D32, J2.pin7
  N37: Arduino_Mega2560.D33, J1.pin7
  N38: Arduino_Mega2560.D34, J2.pin8
  N39: Arduino_Mega2560.D35, J1.pin8
  N40: Arduino_Mega2560.D36, J2.pin9
  N41: Arduino_Mega2560.D37, J1.pin9
  N42: Arduino_Mega2560.D38, J2.pin10
  N43: Arduino_Mega2560.D39, J1.pin10
  N44: Arduino_Mega2560.D40, J2.pin11
  N45: Arduino_Mega2560.D41, J1.pin11
  N46: Arduino_Mega2560.D42, J2.pin12
  N47: Arduino_Mega2560.D43, J1.pin12
  N48: Arduino_Mega2560.D44, J2.pin13
  N49: Arduino_Mega2560.D45, J1.pin13
  N50: Arduino_Mega2560.D46, J2.pin14
  N51: Arduino_Mega2560.D47, J1.pin14
  N52: Arduino_Mega2560.D48, J2.pin15
  N53: Arduino_Mega2560.D49, J1.pin15
  N54: Arduino_Mega2560.D50, J2.pin16
  N55: Arduino_Mega2560.D51, J1.pin16
  N56: Arduino_Mega2560.D52, J2.pin17
  N57: Arduino_Mega2560.D53, J1.pin17
  N58: HC-12.Set, J9.pin1
  N59: L293D.Out_1_(_Controlled_by_Enable_1_), J6.pin1
  N60: L293D.Out_2_(_Controlled_by_Enable_1_), J6.pin2
  N61: L293D.+Vmotor, J8.pin1
  N62: L293D.Out_3_(_Controlled_by_Enable_2_), J7.pin1
  N63: L293D.Out_4_(_Controlled_by_Enable_2_), J7.pin2

custom parts:
  HC-12 Connector: Generic female header
  Generic female header - 7 pins: Generic female header
